# Fritzing sketch input-buffer (saved by Fritzing 1.0.6)
breadboards: 1

parts:
  IC1 = DIP - 8 pins [chip_label=TL072 package="DIP (Dual Inline) [THT]"]
  C_VREF_FILTER = Ceramic Capacitor [capacitance=10µF voltage=35V package="100 mil [THT, multilayer]"]
  C_INPUT_COUPLING = Ceramic Capacitor [capacitance=100nF voltage=35V package="100 mil [THT, multilayer]"]
  LINE_IN = Audio Jack (TRS) 3.5mm [package="4Ucon 08780 [THT]"]
  C_LF_SHAPING = Ceramic Capacitor [capacitance=4.7µF voltage=35V package="100 mil [THT, multilayer]"]
  TO_TEENSY = Audio Jack (TRS) 3.5mm [package="4Ucon 08780 [THT]"]
  C_OUTPUT_COUPLING = Ceramic Capacitor [capacitance=4.7µF voltage=35V package="100 mil [THT, multilayer]"]
  R_GAIN_SET = Resistor [tolerance=±1% power=0.25W resistance=10k package=THT]
  R_OUT_RIGHT = Resistor [tolerance=±1% power=0.25W resistance=330 package=THT]
  R_OUT_LEFT = Resistor [tolerance=±1% power=0.25W resistance=330 package=THT]
  R_FEEDBACK = Resistor [tolerance=±1% power=0.25W resistance=33k package=THT]
  R_IN = Resistor [tolerance=±1% power=0.25W resistance=1M package=THT]
  R_VREF_TOP = Resistor [tolerance=±1% power=0.25W resistance=47k package=THT]
  R_VREF_BOTTOM = Resistor [tolerance=±1% power=0.25W resistance=47k package=THT]
  R1 = Resistor [tolerance=±5% power=0.25W resistance=100k package=THT]

nets:
  N1: IC1.1OUT, C_OUTPUT_COUPLING.0, R_FEEDBACK.Pin_0
  N2: IC1.1IN-, R_GAIN_SET.Pin_0, R_FEEDBACK.Pin_1
  N3: IC1.1IN+, C_INPUT_COUPLING.1, R_IN.Pin_1
  N4: IC1.VCC-, C_VREF_FILTER.0, LINE_IN.Sleeve, C_LF_SHAPING.1, TO_TEENSY.Sleeve, R_VREF_BOTTOM.Pin_0
  N5: C_VREF_FILTER.1, R_IN.Pin_0, R_VREF_BOTTOM.Pin_1
  N6: C_INPUT_COUPLING.0, LINE_IN.Tip
  N7: C_LF_SHAPING.0, R_GAIN_SET.Pin_1
  N8: TO_TEENSY.Ring, R_OUT_RIGHT.Pin_1
  N9: TO_TEENSY.Tip, R_OUT_LEFT.Pin_1
  N10: C_OUTPUT_COUPLING.1, R_OUT_RIGHT.Pin_0, R_OUT_LEFT.Pin_0, R1.Pin_1
  N11: R_VREF_TOP.Pin_0, R1.Pin_0

custom parts:
  DIP - 8 pins: A DIP stand-in part for whatever IC you want. With 8 pins on a 300mil dual inline package (DIP) footprint.
