# Fritzing sketch output-buffer (saved by Fritzing 1.0.6)
breadboards: 1

parts:
  IC1 = DIP - 8 pins [chip_label=IC package="DIP (Dual Inline) [THT]"]
  C_OUT_COUPLING = Ceramic Capacitor [capacitance=4.7µF voltage=35V package="100 mil [THT, multilayer]"]
  R_OUT_BLEED = Resistor [tolerance=±5% power=0.25W resistance=100k package=THT]
  R_OUT = Resistor [tolerance=±5% power=0.25W resistance=330 package=THT]
  TRS1 = Audio Jack (TRS) 3.5mm [package="4Ucon 08780 [THT]"]
  R_VREF_IN = Resistor [tolerance=±5% power=0.25W resistance=1M package=THT]
  R_VREF_TOP = Resistor [tolerance=±5% power=0.25W resistance=47k package=THT]
  R_VREF_BOTTOM = Resistor [tolerance=±5% power=0.25W resistance=47k package=THT]
  R_VIN_TOP = Resistor [tolerance=±5% power=0.25W resistance=47k package=THT]
  R_VIN_BOTTOM = Resistor [tolerance=±5% power=0.25W resistance=47k package=THT]
  C_VREF_FILTER = Ceramic Capacitor [capacitance=10µ voltage=35V package="100 mil [THT, multilayer]"]
  C_IN_COUPLING = Ceramic Capacitor [capacitance=2.2µ voltage=35V package="100 mil [THT, multilayer]"]
  TRS2 = Audio Jack (TRS) 3.5mm [package="4Ucon 08780 [THT]"]

nets:
  N1: IC1.VCC-, R_OUT_BLEED.Pin_0, TRS1.Sleeve, R_VREF_BOTTOM.Pin_1, R_VIN_BOTTOM.Pin_1, C_VREF_FILTER.1, TRS2.Sleeve
  N2: IC1.2IN+, R_VREF_IN.Pin_0, C_IN_COUPLING.0
  N3: IC1.2IN-, IC1.2OUT, C_OUT_COUPLING.1
  N4: IC1.VCC+, R_VREF_TOP.Pin_1
  N5: C_OUT_COUPLING.0, R_OUT_BLEED.Pin_1, R_OUT.Pin_1
  N6: R_OUT.Pin_0, TRS1.Tip
  N7: R_VREF_IN.Pin_1, R_VREF_TOP.Pin_0, R_VREF_BOTTOM.Pin_0, C_VREF_FILTER.0
  N8: R_VIN_TOP.Pin_0, R_VIN_BOTTOM.Pin_0, C_IN_COUPLING.1
  N9: R_VIN_TOP.Pin_1, TRS2.Tip

notes:
  Input
  Output
  Biasing Network

custom parts:
  DIP - 8 pins: A DIP stand-in part for whatever IC you want. With 8 pins on a 300mil dual inline package (DIP) footprint.
